// Logisim project Microprocessor.circ as structural Verilog: 1 circuit, main circuit CPU
module CPU (
);

  wire alu_1_p21, alu_1_p23, alu_1_p24, alu_1_p25, alu_1_p26, alu_1_p27, clock_1_out, control_unit_1_p1,
       control_unit_1_p2, control_unit_1_p26, control_unit_1_p27, flag_1_p1, flag_1_p2, flag_1_p3, flag_1_p4,
       flag_1_p5, flag_2_p1, flag_2_p3, flag_2_p4, flag_2_p5, instruction_register_1_p2,
       special_purpose_1_p3, special_purpose_2_p2, special_purpose_2_p3, special_purpose_3_p3, undriven,
       undriven_2, undriven_3, undriven_4, undriven_5, undriven_6, undriven_7, undriven_8, undriven_9;
  wire [2:0] control_unit_1_p28;
  wire [4:0] control_unit_1_p3;
  wire [6:0] control_unit_1_p19;
  wire [7:0] instruction_register_1_p4;
  wire [8:0] general_purpose_1_p10, general_purpose_2_p10, general_purpose_3_p10, general_purpose_4_p10,
       general_purpose_5_p10;
  wire [10:0] control_unit_1_p18;
  wire [15:0] alu_1_p16, alu_1_p17, alu_1_p18, alu_1_p19, alu_1_p20, alu_1_p22, multiplexer_1_out,
       special_purpose_1_p5, special_purpose_2_p5;
  wire [23:0] controlled_buffer_1_out, ram_1_data;

  // CONTROL_UNIT control_unit_1: pin names not known; wires that end beside it: control_unit_1_p1, control_unit_1_p2, control_unit_1_p3[0], control_unit_1_p3[1], control_unit_1_p3[2], control_unit_1_p3[3], control_unit_1_p3[4], control_unit_1_p18[10], control_unit_1_p18[9], control_unit_1_p18[8], control_unit_1_p18[7], control_unit_1_p18[6], control_unit_1_p18[5], control_unit_1_p18[4], control_unit_1_p18[3], control_unit_1_p18[2], control_unit_1_p18[1], control_unit_1_p18[0], control_unit_1_p19[0], control_unit_1_p19[1], control_unit_1_p19[2], control_unit_1_p19[3], control_unit_1_p19[4], control_unit_1_p19[5], control_unit_1_p19[6], control_unit_1_p26, control_unit_1_p27, control_unit_1_p28, general_purpose_1_p10[8], general_purpose_1_p10[6], general_purpose_1_p10[5], general_purpose_1_p10[4], general_purpose_1_p10[3], general_purpose_1_p10[2], general_purpose_1_p10[1]
  Clock clock_1 (.out(clock_1_out));
  // FLAG flag_1: pin names not known; wires that end beside it: flag_1_p1, flag_1_p2, flag_1_p3, flag_1_p4, flag_1_p5, control_unit_1_p2
  and and_1 (flag_1_p2, ~undriven, clock_1_out);  // AND_Gate
  // FLAG flag_2: pin names not known; wires that end beside it: flag_2_p1, flag_1_p2, flag_2_p3, flag_2_p4, flag_2_p5, control_unit_1_p1
  // ALU alu_1: pin names not known; wires that end beside it: control_unit_1_p1, control_unit_1_p3[0], control_unit_1_p3[1], control_unit_1_p3[2], control_unit_1_p3[3], control_unit_1_p3[4], 1'b0, 1'b0, control_unit_1_p19[0], control_unit_1_p19[1], control_unit_1_p19[2], control_unit_1_p19[3], control_unit_1_p19[4], control_unit_1_p19[5], control_unit_1_p19[6], alu_1_p16, alu_1_p17, alu_1_p18, alu_1_p19, alu_1_p20, alu_1_p21, alu_1_p22, alu_1_p23, alu_1_p24, alu_1_p25, alu_1_p26, alu_1_p27, flag_1_p1, flag_2_p1
  // GENERAL_PURPOSE general_purpose_1: pin names not known; wires that end beside it: alu_1_p23, general_purpose_1_p10[8], general_purpose_1_p10[7], general_purpose_1_p10[6], general_purpose_1_p10[5], general_purpose_1_p10[4], general_purpose_1_p10[3], general_purpose_1_p10[2], general_purpose_1_p10[1], general_purpose_1_p10[0], flag_1_p2, alu_1_p16
  // GENERAL_PURPOSE general_purpose_2: pin names not known; wires that end beside it: alu_1_p24, general_purpose_2_p10[8], general_purpose_2_p10[7], general_purpose_2_p10[6], general_purpose_2_p10[5], general_purpose_2_p10[4], general_purpose_2_p10[3], general_purpose_2_p10[2], general_purpose_2_p10[1], general_purpose_2_p10[0], flag_1_p2, alu_1_p17
  // GENERAL_PURPOSE general_purpose_3: pin names not known; wires that end beside it: alu_1_p25, general_purpose_3_p10[8], general_purpose_3_p10[7], general_purpose_3_p10[6], general_purpose_3_p10[5], general_purpose_3_p10[4], general_purpose_3_p10[3], general_purpose_3_p10[2], general_purpose_3_p10[1], general_purpose_3_p10[0], flag_1_p2, alu_1_p18
  // GENERAL_PURPOSE general_purpose_4: pin names not known; wires that end beside it: alu_1_p26, general_purpose_4_p10[8], general_purpose_4_p10[7], general_purpose_4_p10[6], general_purpose_4_p10[5], general_purpose_4_p10[4], general_purpose_4_p10[3], general_purpose_4_p10[2], general_purpose_4_p10[1], general_purpose_4_p10[0], flag_1_p2, alu_1_p19
  // GENERAL_PURPOSE general_purpose_5: pin names not known; wires that end beside it: alu_1_p27, general_purpose_5_p10[8], general_purpose_5_p10[7], general_purpose_5_p10[6], general_purpose_5_p10[5], general_purpose_5_p10[4], general_purpose_5_p10[3], general_purpose_5_p10[2], general_purpose_5_p10[1], general_purpose_5_p10[0], flag_1_p2, alu_1_p20, alu_1_p20
  Multiplexer #(.select(3), .width(16), .enable("false")) multiplexer_1 (
    .in0(special_purpose_1_p5), .in1(alu_1_p16), .in2(alu_1_p17), .in3(alu_1_p18), .in4(alu_1_p19),
    .in5(alu_1_p20), .out(multiplexer_1_out), .sel(control_unit_1_p28));  // open: in6, in7
  assign controlled_buffer_1_out = undriven_4 ? {{8{1'b0}}, alu_1_p16} : 24'bz;  // Controlled_Buffer controlled_buffer_1
  assign controlled_buffer_1_out = undriven_5 ? {{8{1'b0}}, alu_1_p17} : 24'bz;  // Controlled_Buffer controlled_buffer_2
  assign controlled_buffer_1_out = undriven_6 ? {{8{1'b0}}, alu_1_p18} : 24'bz;  // Controlled_Buffer controlled_buffer_3
  assign controlled_buffer_1_out = undriven_7 ? {{8{1'b0}}, alu_1_p19} : 24'bz;  // Controlled_Buffer controlled_buffer_4
  assign controlled_buffer_1_out = undriven_2 ? {{8{1'b0}}, alu_1_p20} : 24'bz;  // Controlled_Buffer controlled_buffer_5
  // SPECIAL_PURPOSE special_purpose_1: pin names not known; wires that end beside it: controlled_buffer_1_out[15:0], 1'b0, special_purpose_1_p3, flag_1_p2, special_purpose_1_p5
  // SPECIAL_PURPOSE special_purpose_2: pin names not known; wires that end beside it: controlled_buffer_1_out[15:0], special_purpose_2_p2, special_purpose_2_p3, flag_1_p2, special_purpose_2_p5
  // SPECIAL_PURPOSE special_purpose_3: pin names not known; wires that end beside it: controlled_buffer_1_out[15:0], 1'b0, special_purpose_3_p3, flag_1_p2, alu_1_p21
  // INSTRUCTION_REGISTER instruction_register_1: pin names not known; wires that end beside it: controlled_buffer_1_out, instruction_register_1_p2, flag_1_p2, {instruction_register_1_p4, alu_1_p22}
  RAM #(.addrWidth(16), .dataWidth(24), .bus("separate")) ram_1 (
    .addr(multiplexer_1_out), .din(controlled_buffer_1_out), .data(ram_1_data), .str(control_unit_1_p26),
    .clk(flag_1_p2));  // open: sel, ld, clr
  assign controlled_buffer_1_out = control_unit_1_p27 ? ram_1_data : 24'bz;  // Controlled_Buffer controlled_buffer_6
  assign controlled_buffer_1_out = undriven_9 ? {{8{1'b0}}, special_purpose_1_p5} : 24'bz;  // Controlled_Buffer controlled_buffer_7
  assign controlled_buffer_1_out = undriven_3 ? {{8{1'b0}}, special_purpose_2_p5} : 24'bz;  // Controlled_Buffer controlled_buffer_8
  assign controlled_buffer_1_out = undriven_8 ? {instruction_register_1_p4, alu_1_p22} : 24'bz;  // Controlled_Buffer controlled_buffer_9

  // Notes on the sheet:
  //   ZF
  //   CF
  //   ALU
  //   AX
  //   BX
  //   CX
  //   DX
  //   EX
  //   AR
  //   PC
  //   DR
  //   IR
endmodule
